# Fritzing sketch Automatic Street Lights With Intensity Control (saved by Fritzing 0.9.3b)
breadboards: 2

parts:
  Part1 = Arduino Uno (Rev3)
  hc-sr3 = hc-sr04
  hc-sr1 = hc-sr04
  hc-sr4 = hc-sr04
  LED1 = LEDs [package=led10mm]
  LED2 = LEDs [package=led10mm]
  LED3 = LEDs [package=led10mm]
  R1 = Photocell (LDR) [package=THT]
  R2 = Resistor [tolerance=±5% resistance=100k package="0603 [SMD]"]

nets:
  N1: Part1.A0, R1.pin_1, R2.Pin_1
  N2: Part1.D8, hc-sr1.Trig
  N3: Part1.D10_PWM/SS, LED2.A
  N4: Part1.D11_PWM/MOSI, LED3.A
  N5: Part1.D12/MISO, hc-sr3.Echo
  N6: Part1.D13/SCK, hc-sr3.Trig
  N7: Part1.D2, hc-sr4.Echo
  N8: Part1.D4, hc-sr4.Trig
  N9: Part1.D6_PWM, LED1.A
  N10: Part1.D7, hc-sr1.Echo
  VCC: Part1.5V, hc-sr3.VCC, hc-sr1.VCC, hc-sr4.VCC
  GND: Part1.GND, hc-sr3.GND, hc-sr1.GND, hc-sr4.GND, R2.Pin_0
  N11: LED1.C, LED2.C, LED3.C
